# Fritzing sketch indoorcircuit (saved by Fritzing 0.9.4)
breadboards: 1

parts:
  U2 = NodeMCU V1.0
  R1 = Resistor [tolerance=±5% resistance=220 package=THT]
  IR1 = TSOP312.., 314.. [package=THT]
  R2 = Photocell (LDR) [package=THT]
  R3 = Resistor [tolerance=±5% resistance=10k package=THT]
  LED1 = smd LED [color="Red (633nm)" package="0603 [SMD]"]

nets:
  N1: U2.D1, LED1.anode
  N2: U2.3V3, IR1.Data, R2.pin_1
  N3: U2.GND, R1.Pin_1, IR1.Vs, R3.Pin_1
  N4: U2.D5, IR1.GND
  N5: U2.A0, R2.pin_0, R3.Pin_0
  N6: R1.Pin_0, LED1.cathode

custom parts:
  NodeMCU V1.0: ESP8266 based NodeMCU
