# Fritzing sketch wallcircuit (saved by Fritzing 0.9.4)
breadboards: 2

parts:
  A1 = Arduino Nano ESP32
  R1 = Resistor [tolerance=±5% resistance=10k package="0402 [SMD]"]
  R2 = PHOTOCELL [package=photocell-kit]
  LED2 = smd LED [color="Blue (430nm)" package="0603 [SMD]"]
  LED3 = smd LED [color="Blue (430nm)" package="0603 [SMD]"]
  LED1 = smd LED [color="Blue (430nm)" package="0603 [SMD]"]
  R3 = Resistor [tolerance=±5% resistance=220 package="0402 [SMD]"]

nets:
  N1: A1.Pin_2, R2.P$2
  N2: A1.Pin_4, R1.Pin_1, R2.P$1
  N3: A1.Pin_14, A1.Pin_19, R1.Pin_0, R3.Pin_0
  N4: A1.Pin_21, LED2.anode, LED3.anode, LED1.anode
  N5: LED2.cathode, LED3.cathode, LED1.cathode, R3.Pin_1

custom parts:
  Arduino Nano ESP32: Arduino® Nano ESP32 tht.
