# Fritzing sketch windowcircuit (saved by Fritzing 0.9.4)
breadboards: 1

parts:
  A2 = Arduino Nano ESP32
  J1 = Basic Servo
  R1 = Trimmer Potentiometer [maximum_resistance=10kΩ package=THT]

nets:
  N1: A2.Pin_2, J1.vcc, R1.leg2
  N2: A2.Pin_4, R1.wiper
  N3: A2.Pin_14, A2.Pin_19, J1.gnd, R1.leg1
  N4: A2.Pin_23, J1.pulse

custom parts:
  Arduino Nano ESP32: Arduino® Nano ESP32 tht.
